# Fritzing sketch sketch (saved by Fritzing 0.9.3b)
circuit board: 10cm x 7cm
breadboards: 2

parts:
  Part1 = Motor Driver 1A Dual TB6612FNG
  U1 = NodeMCU V1.0
  Omega = female pin header, 2 pins [form="♀ (female)"]
  Rolex = female pin header, 2 pins [form="♀ (female)"]
  PWR = female pin header, 2 pins [form="♀ (female)"]
  On = female pin header, 2 pins [form="♀ (female)"]

nets:
  GND: Part1.GND, U1.GND, PWR.pin2
  N1: Part1.B01, Omega.pin1
  N2: Part1.B02, Omega.pin2
  N3: Part1.A02, Rolex.pin1
  N4: Part1.A01, Rolex.pin2
  VCC: Part1.VCC, U1.3V3
  N5: Part1.VM, U1.Vin, On.pin2
  N6: Part1.PWMA, U1.D8
  N7: Part1.AIN2, U1.D7
  N8: Part1.AIN1, U1.D6
  N9: Part1.STBY, U1.D5
  N10: Part1.BIN1, U1.D4
  N11: Part1.BIN2, U1.D2
  N12: Part1.PWMB, U1.D1
  N13: PWR.pin1, On.pin1

custom parts:
  NodeMCU V1.0: ESP8266 based NodeMCU
